// Logisim project halfAdder_broken.circ as structural Verilog: 1 circuit, main circuit main
module main (
  input  InputA,
  input  InputB,
  output Sum,
  output Carry
);

  xor xor_1 (Sum, InputA, InputB);
  or or_1 (Carry, InputA, InputB);
endmodule
